// Logisim project CPU.circ as structural Verilog: 4 circuits, main circuit main
module main (
  input  A1,
  input  [7:0] Store_Data,
  input  A2,
  input  Store,
  input  in_out,
  input  in_6,
  input  [3:0] Address,
  input  [7:0] in_8,
  input  in_9,
  input  write_enable,
  input  in_11,
  input  Clock,
  input  in_13,
  input  read_enable,
  input  in_15,
  input  in_16,
  input  in_17,
  input  in_18,
  input  [7:0] in_19,
  input  in_20,
  input  Read,
  input  in_22,
  input  Write,
  input  in_24,
  input  En,
  input  in_26,
  input  Override,
  input  [3:0] Address_2,
  input  in_29,
  input  [1:0] in_30,
  input  Clear,
  input  Clock_2,
  input  Clock_3,
  input  [7:0] Store_Data_2,
  input  [3:0] Address_3,
  input  Store_2,
  input  [2:0] Address_4,
  input  Clock_4,
  input  in_39,
  input  [2:0] in_40,
  input  in_41,
  input  Clock_5,
  input  [7:0] in_43,
  output out_44,
  output [7:0] out_45,
  output out_46,
  output out_47,
  output [7:0] Load_Store_Data,
  output out_49,
  output out_50,
  output [7:0] out_51,
  output [7:0] out_52,
  output out_53,
  output out_54,
  output [1:0] out_55,
  output [7:0] Load_Store_Data_2,
  output [2:0] out_57,
  output [7:0] out_58
);

  wire and_5_out, and_6_out, and_7_out, and_8_out, and_9_out, and_10_out, decoder_1_out_3, decoder_1_out_4,
       decoder_1_out_5, decoder_1_out_6, decoder_2_out_3, decoder_2_out_4, decoder_2_out_5, decoder_2_out_6,
       decoder_3_out_3, decoder_3_out_4, decoder_3_out_5, decoder_3_out_6, decoder_4_out_3, decoder_4_out_4,
       decoder_4_out_5, decoder_5_out_3, decoder_5_out_4, decoder_5_out_5, decoder_5_out_6, decoder_6_out_3,
       decoder_6_out_4, decoder_6_out_5, decoder_6_out_6, gated_latch_10_out_3, not_1_out, not_2_out,
       not_3_out, not_4_out, not_5_out, not_6_out, not_7_out, not_8_out, or_1_out, or_2_out, or_3_out,
       or_4_out, or_5_out;
  wire [1:0] controlled_buffer_9_out;
  wire [7:0] adder_1_out, controlled_buffer_1_out, controlled_buffer_2_out, controlled_buffer_3_out,
       controlled_buffer_4_out, controlled_buffer_5_out, controlled_buffer_6_out, controlled_buffer_7_out,
       controlled_buffer_8_out, controlled_buffer_11_out, controlled_buffer_12_out, controlled_buffer_13_out,
       controlled_buffer_15_out, controlled_buffer_16_out, controlled_buffer_17_out,
       controlled_buffer_18_out, controlled_buffer_19_out, divider_1_out, multiplexer_3_out,
       multiplexer_4_out, multiplexer_5_out, multiplier_1_out, register_1_q, register_2_q, register_3_q,
       register_4_q, register_5_q, subtractor_1_out;

  // Probe on multiplexer_3_out
  Multiplexer #(.select(2), .enable("false")) multiplexer_1 (
    .in0(in_22), .in1(in_24), .in2(in_26), .in3(in_29), .out(out_50), .sel(in_30));
  assign controlled_buffer_1_out = decoder_1_out_6 ? multiplexer_4_out : 8'bz;  // Controlled_Buffer controlled_buffer_1
  Multiplier multiplier_1 (
    .a(controlled_buffer_1_out), .b(controlled_buffer_2_out), .out(multiplier_1_out), .cout(out_51));  // open: cin
  assign controlled_buffer_2_out = decoder_1_out_6 ? multiplexer_3_out : 8'bz;  // Controlled_Buffer controlled_buffer_2
  assign controlled_buffer_3_out = decoder_1_out_5 ? multiplexer_4_out : 8'bz;  // Controlled_Buffer controlled_buffer_3
  Divider divider_1 (
    .a(controlled_buffer_3_out), .b(controlled_buffer_4_out), .out(divider_1_out), .rem(out_52));  // open: upper
  assign controlled_buffer_4_out = decoder_1_out_5 ? multiplexer_3_out : 8'bz;  // Controlled_Buffer controlled_buffer_4
  assign controlled_buffer_5_out = decoder_1_out_4 ? multiplexer_4_out : 8'bz;  // Controlled_Buffer controlled_buffer_5
  Subtractor subtractor_1 (
    .a(controlled_buffer_5_out), .b(controlled_buffer_6_out), .out(subtractor_1_out), .bout(out_53));  // open: bin
  assign controlled_buffer_6_out = decoder_1_out_4 ? multiplexer_3_out : 8'bz;  // Controlled_Buffer controlled_buffer_6
  assign controlled_buffer_7_out = decoder_1_out_3 ? multiplexer_4_out : 8'bz;  // Controlled_Buffer controlled_buffer_7
  Adder adder_1 (
    .a(controlled_buffer_7_out), .b(controlled_buffer_8_out), .out(adder_1_out), .cout(out_54));  // open: cin
  assign controlled_buffer_8_out = decoder_1_out_3 ? multiplexer_3_out : 8'bz;  // Controlled_Buffer controlled_buffer_8
  // Probe on multiplexer_4_out
  // Probe on controlled_buffer_9_out
  Decoder decoder_1 (
    .in_1(controlled_buffer_9_out[0]), .in_2(controlled_buffer_9_out[1]), .out_3(decoder_1_out_3),
    .out_4(decoder_1_out_4), .out_5(decoder_1_out_5), .out_6(decoder_1_out_6));
  assign controlled_buffer_9_out[0] = decoder_4_out_3 ? in_43[5] : 1'bz;  // Controlled_Buffer controlled_buffer_9
  // Probe on in_43[3:2]
  Multiplexer #(.select(2), .width(8), .enable("false")) multiplexer_2 (
    .in0(adder_1_out), .in1(divider_1_out), .in2(subtractor_1_out), .in3(multiplier_1_out), .out(out_58),
    .sel(controlled_buffer_9_out));
  assign controlled_buffer_9_out[1] = decoder_4_out_3 ? in_43[4] : 1'bz;  // Controlled_Buffer controlled_buffer_10
  not not_1 (not_1_out, in_6);
  not not_2 (not_2_out, in_13);
  assign controlled_buffer_11_out = or_1_out ? register_1_q : 8'bz;  // Controlled_Buffer controlled_buffer_11
  Register register_1 (.D(controlled_buffer_15_out), .en(or_1_out), .Q(register_1_q), .clk(Clock_3));  // open: clr
  or or_1 (or_1_out, decoder_2_out_3, decoder_3_out_3);
  Decoder decoder_2 (
    .in_1(in_43[3]), .in_2(in_43[2]), .out_3(decoder_2_out_3), .out_4(decoder_2_out_4),
    .out_5(decoder_2_out_5), .out_6(decoder_2_out_6));
  assign controlled_buffer_12_out = Override ? in_19 : 8'bz;  // Controlled_Buffer controlled_buffer_12
  Multiplexer #(.select(2), .width(8), .enable("false")) multiplexer_3 (
    .in0(controlled_buffer_11_out), .in1(controlled_buffer_13_out), .in2(controlled_buffer_16_out),
    .in3(controlled_buffer_17_out), .out(multiplexer_3_out), .sel(in_43[3:2]));
  assign controlled_buffer_13_out = or_2_out ? register_2_q : 8'bz;  // Controlled_Buffer controlled_buffer_13
  Register register_2 (.D(controlled_buffer_15_out), .en(or_2_out), .Q(register_2_q), .clk(Clock_3));  // open: clr
  or or_2 (or_2_out, decoder_2_out_4, decoder_3_out_4);
  or or_3 (or_3_out, decoder_2_out_5, decoder_3_out_5);
  Decoder decoder_3 (
    .in_1(in_43[1]), .in_2(in_43[0]), .out_3(decoder_3_out_3), .out_4(decoder_3_out_4),
    .out_5(decoder_3_out_5), .out_6(decoder_3_out_6));
  assign controlled_buffer_12_out = Read ? controlled_buffer_19_out : 8'bz;  // Controlled_Buffer controlled_buffer_14
  Multiplexer #(.select(2), .width(8), .enable("false")) multiplexer_4 (
    .in0(controlled_buffer_11_out), .in1(controlled_buffer_13_out), .in2(controlled_buffer_16_out),
    .in3(controlled_buffer_17_out), .out(multiplexer_4_out), .sel(in_43[1:0]));
  assign controlled_buffer_15_out = decoder_4_out_4 ? controlled_buffer_18_out : 8'bz;  // Controlled_Buffer controlled_buffer_15
  assign controlled_buffer_16_out = or_3_out ? register_3_q : 8'bz;  // Controlled_Buffer controlled_buffer_16
  Register register_3 (.D(controlled_buffer_15_out), .en(or_3_out), .Q(register_3_q), .clk(Clock_3));  // open: clr
  or or_4 (or_4_out, decoder_2_out_6, decoder_3_out_6);
  and and_1 (out_44, not_1_out, not_2_out);
  and and_2 (out_46, not_1_out, in_13);
  and and_3 (out_47, in_6, not_2_out);
  and and_4 (out_49, in_13, in_6);
  assign controlled_buffer_17_out = or_4_out ? register_4_q : 8'bz;  // Controlled_Buffer controlled_buffer_17
  Register register_4 (.D(controlled_buffer_15_out), .en(or_4_out), .Q(register_4_q), .clk(Clock_3));  // open: clr
  Decoder decoder_4 (
    .in_1(in_43[7]), .in_2(in_43[6]), .out_3(decoder_4_out_3), .out_4(decoder_4_out_4),
    .out_5(decoder_4_out_5));  // open: out_6
  Register register_5 (.D(controlled_buffer_12_out), .en(En), .Q(register_5_q), .clk(Clock_2), .clr(Clear));
  not not_3 (not_3_out, in_9);
  // Probe on multiplexer_5_out
  Multiplexer #(.select(2), .width(8), .enable("false")) multiplexer_5 (
    .in0(controlled_buffer_11_out), .in1(controlled_buffer_13_out), .in2(controlled_buffer_16_out),
    .in3(controlled_buffer_17_out), .out(multiplexer_5_out), .sel(in_43[1:0]));
  assign controlled_buffer_18_out = decoder_4_out_5 ? multiplexer_5_out : 8'bz;  // Controlled_Buffer controlled_buffer_18
  and and_5 (and_5_out, in_11, in_9);
  and and_6 (and_6_out, not_3_out, in_11);
  not not_4 (not_4_out, and_6_out);
  Gated_Latch gated_latch_1 ();  // open: in_1, in_2, out_3
  not not_5 (not_5_out, decoder_4_out_5);
  or or_5 (or_5_out, and_7_out, and_5_out);
  and and_7 (and_7_out, or_5_out, not_4_out);
  RAM #(.addrWidth(4)) ram_1 (
    .addr(Address_3), .data(controlled_buffer_18_out), .clk(Clock_3), .ld(not_5_out));  // open: sel, clr
  assign controlled_buffer_19_out = Write ? register_5_q : 8'bz;  // Controlled_Buffer controlled_buffer_19
  Gated_Latch gated_latch_2 (.in_1(in_8[0]), .in_2(in_15), .out_3(out_45[0]));
  Gated_Latch gated_latch_3 (.in_1(in_8[1]), .in_2(in_15), .out_3(out_45[1]));
  Gated_Latch gated_latch_4 (.in_1(in_8[2]), .in_2(in_15), .out_3(out_45[2]));
  Gated_Latch gated_latch_5 (.in_1(in_8[3]), .in_2(in_15), .out_3(out_45[3]));
  Gated_Latch gated_latch_6 (.in_1(in_8[4]), .in_2(in_15), .out_3(out_45[4]));
  Gated_Latch gated_latch_7 (.in_1(in_8[5]), .in_2(in_15), .out_3(out_45[5]));
  Gated_Latch gated_latch_8 (.in_1(in_8[6]), .in_2(in_15), .out_3(out_45[6]));
  Gated_Latch gated_latch_9 (.in_1(in_8[7]), .in_2(in_15), .out_3(out_45[7]));
  _8_bit_Register u_8_bit_register_1 ();  // open: in_1, out_3, in_2
  not not_6 (not_6_out, Write);
  Counter #(.width(3), .max('h7)) counter_1 (
    .load(in_39), .D(in_40), .count(in_41), .Q(out_57), .clk(Clock_5));  // open: carry, clr
  RAM #(.addrWidth(4)) ram_2 (
    .addr(Address_2), .data(controlled_buffer_19_out), .clk(Clock_2), .ld(not_6_out));  // open: sel, clr
  assign Load_Store_Data_2 = Store_2 ? Store_Data_2 : 8'bz;  // Controlled_Buffer controlled_buffer_20
  not not_7 (not_7_out, Store_2);
  assign Load_Store_Data = Store ? Store_Data : 8'bz;  // Controlled_Buffer controlled_buffer_21
  Decoder decoder_5 (
    .in_1(in_16), .in_2(in_17), .out_3(decoder_5_out_3), .out_4(decoder_5_out_4), .out_5(decoder_5_out_5),
    .out_6(decoder_5_out_6));
  Decoder decoder_6 (
    .in_1(in_18), .in_2(in_20), .out_3(decoder_6_out_3), .out_4(decoder_6_out_4), .out_5(decoder_6_out_5),
    .out_6(decoder_6_out_6));
  RAM #(.addrWidth(3)) ram_3 (
    .addr(Address_4), .data(Load_Store_Data_2), .clk(Clock_4), .ld(not_7_out));  // open: sel, clr
  not not_8 (not_8_out, Store);
  RAM #(.addrWidth(4)) ram_4 (.addr(Address), .data(Load_Store_Data), .clk(Clock), .ld(not_8_out));  // open: sel, clr
  and and_8 (and_8_out, A1, A2);
  and and_9 (and_9_out, and_8_out, write_enable);
  and and_10 (and_10_out, and_8_out, read_enable);
  Gated_Latch gated_latch_10 (.in_1(in_out), .in_2(and_9_out), .out_3(gated_latch_10_out_3));
  Transistor #(.\type ("n"), .gate("br")) transistor_1 (.in(gated_latch_10_out_3), .out(in_out), .gate(and_10_out));

  assign out_55 = in_43[1:0];

  // Notes on the sheet:
  //   Decoder
  //   Load
  //   Set Register
  //   Store
  //   Gated Latch
  //   8-bit Register
  //   SRAM
endmodule

module Decoder (
  input  in_1,
  input  in_2,
  output out_3,
  output out_4,
  output out_5,
  output out_6
);

  wire not_1_out, not_2_out;

  not not_1 (not_1_out, in_1);
  not not_2 (not_2_out, in_2);
  and and_1 (out_3, not_1_out, not_2_out);
  and and_2 (out_4, not_1_out, in_2);
  and and_3 (out_5, in_1, not_2_out);
  and and_4 (out_6, in_2, in_1);
endmodule

module Gated_Latch (
  input  in_1,
  input  in_2,
  output out_3
);

  wire and_1_out, and_2_out, not_1_out, not_2_out, or_1_out;

  not not_1 (not_1_out, in_1);
  and and_1 (and_1_out, in_2, in_1);
  not not_2 (not_2_out, and_2_out);
  and and_2 (and_2_out, not_1_out, in_2);
  or or_1 (or_1_out, out_3, and_1_out);
  and and_3 (out_3, or_1_out, not_2_out);
endmodule

module _8_bit_Register (
  input  [7:0] in_1,
  input  in_2,
  output [7:0] out_3
);

  Gated_Latch gated_latch_1 (.in_1(in_1[0]), .in_2(in_2), .out_3(out_3[0]));
  Gated_Latch gated_latch_2 (.in_1(in_1[1]), .in_2(in_2), .out_3(out_3[1]));
  Gated_Latch gated_latch_3 (.in_1(in_1[2]), .in_2(in_2), .out_3(out_3[2]));
  Gated_Latch gated_latch_4 (.in_1(in_1[3]), .in_2(in_2), .out_3(out_3[3]));
  Gated_Latch gated_latch_5 (.in_1(in_1[4]), .in_2(in_2), .out_3(out_3[4]));
  Gated_Latch gated_latch_6 (.in_1(in_1[5]), .in_2(in_2), .out_3(out_3[5]));
  Gated_Latch gated_latch_7 (.in_1(in_1[6]), .in_2(in_2), .out_3(out_3[6]));
  Gated_Latch gated_latch_8 (.in_1(in_1[7]), .in_2(in_2), .out_3(out_3[7]));

  // Notes on the sheet:
  //   8-bit Register
endmodule
